// Logisim project alu.circ as structural Verilog: 4 circuits, main circuit main
module main (
  input  [31:0] X,
  input  [31:0] Y,
  input  [3:0] Switch,
  output Signed_Overflow,
  output Equal,
  output [31:0] Result
);


  // Other names for the same wires on the sheet: overflow = Signed_Overflow; S[3:0] = Switch

  // Notes on the sheet:
  //   INPUTS to your circuit
  //   DON'T CHANGE THE LOCATIONS OF THE INPUTS AND OUTPUTS!
  //   OUTPUTS from your circuit
endmodule

module sll (
  input  [31:0] B,
  input  [31:0] A,
  output [31:0] out
);

  wire [31:0] multiplexer_1_out, multiplexer_2_out, multiplexer_3_out, multiplexer_4_out, shifter_1_out,
       shifter_2_out, shifter_3_out, shifter_4_out, shifter_5_out;

  Multiplexer #(.width(32)) multiplexer_1 (
    .in0(B), .in1(shifter_1_out), .out(multiplexer_1_out), .sel(A[0]));  // open: en
  Shifter #(.width(32)) shifter_1 (.in(B), .\dist (5'b00001), .out(shifter_1_out));
  Shifter #(.width(32)) shifter_2 (.in(multiplexer_1_out), .\dist (5'b00010), .out(shifter_2_out));
  Multiplexer #(.width(32)) multiplexer_2 (
    .in0(multiplexer_1_out), .in1(shifter_2_out), .out(multiplexer_2_out), .sel(A[1]));  // open: en
  Shifter #(.width(32)) shifter_3 (.in(multiplexer_2_out), .\dist (5'b00100), .out(shifter_3_out));
  Multiplexer #(.width(32)) multiplexer_3 (
    .in0(multiplexer_2_out), .in1(shifter_3_out), .out(multiplexer_3_out), .sel(A[2]));  // open: en
  Shifter #(.width(32)) shifter_4 (.in(multiplexer_3_out), .\dist (5'b01000), .out(shifter_4_out));
  Multiplexer #(.width(32)) multiplexer_4 (
    .in0(multiplexer_3_out), .in1(shifter_4_out), .out(multiplexer_4_out), .sel(A[3]));  // open: en
  Shifter #(.width(32)) shifter_5 (.in(multiplexer_4_out), .\dist (5'b10000), .out(shifter_5_out));
  Multiplexer #(.width(32)) multiplexer_5 (
    .in0(multiplexer_4_out), .in1(shifter_5_out), .out(out), .sel(A[4]));  // open: en
endmodule

module srl (
  input  [31:0] B,
  input  [31:0] A,
  output [31:0] out
);

  wire [31:0] multiplexer_1_out, multiplexer_2_out, multiplexer_3_out, multiplexer_4_out, shifter_1_out,
       shifter_2_out, shifter_3_out, shifter_4_out, shifter_5_out;

  Multiplexer #(.width(32)) multiplexer_1 (
    .in0(B), .in1(shifter_1_out), .out(multiplexer_1_out), .sel(A[0]));  // open: en
  Shifter #(.width(32), .shift("lr")) shifter_1 (.in(B), .\dist (5'b00001), .out(shifter_1_out));
  Shifter #(.width(32), .shift("lr")) shifter_2 (.in(multiplexer_1_out), .\dist (5'b00010), .out(shifter_2_out));
  Multiplexer #(.width(32)) multiplexer_2 (
    .in0(multiplexer_1_out), .in1(shifter_2_out), .out(multiplexer_2_out), .sel(A[1]));  // open: en
  Shifter #(.width(32), .shift("lr")) shifter_3 (.in(multiplexer_2_out), .\dist (5'b00100), .out(shifter_3_out));
  Multiplexer #(.width(32)) multiplexer_3 (
    .in0(multiplexer_2_out), .in1(shifter_3_out), .out(multiplexer_3_out), .sel(A[2]));  // open: en
  Shifter #(.width(32), .shift("lr")) shifter_4 (.in(multiplexer_3_out), .\dist (5'b01000), .out(shifter_4_out));
  Multiplexer #(.width(32)) multiplexer_4 (
    .in0(multiplexer_3_out), .in1(shifter_4_out), .out(multiplexer_4_out), .sel(A[3]));  // open: en
  Shifter #(.width(32), .shift("lr")) shifter_5 (.in(multiplexer_4_out), .\dist (5'b10000), .out(shifter_5_out));
  Multiplexer #(.width(32)) multiplexer_5 (
    .in0(multiplexer_4_out), .in1(shifter_5_out), .out(out), .sel(A[4]));  // open: en
endmodule

module sra (
  input  [31:0] B,
  input  [31:0] A,
  output [31:0] out
);

  wire [31:0] multiplexer_1_out, multiplexer_2_out, multiplexer_3_out, multiplexer_4_out, shifter_1_out,
       shifter_2_out, shifter_3_out, shifter_4_out, shifter_5_out;

  Multiplexer #(.width(32)) multiplexer_1 (
    .in0(B), .in1(shifter_1_out), .out(multiplexer_1_out), .sel(A[0]));  // open: en
  Shifter #(.width(32), .shift("ar")) shifter_1 (.in(B), .\dist (5'b00001), .out(shifter_1_out));
  Shifter #(.width(32), .shift("ar")) shifter_2 (.in(multiplexer_1_out), .\dist (5'b00010), .out(shifter_2_out));
  Multiplexer #(.width(32)) multiplexer_2 (
    .in0(multiplexer_1_out), .in1(shifter_2_out), .out(multiplexer_2_out), .sel(A[1]));  // open: en
  Shifter #(.width(32), .shift("ar")) shifter_3 (.in(multiplexer_2_out), .\dist (5'b00100), .out(shifter_3_out));
  Multiplexer #(.width(32)) multiplexer_3 (
    .in0(multiplexer_2_out), .in1(shifter_3_out), .out(multiplexer_3_out), .sel(A[2]));  // open: en
  Shifter #(.width(32), .shift("ar")) shifter_4 (.in(multiplexer_3_out), .\dist (5'b01000), .out(shifter_4_out));
  Multiplexer #(.width(32)) multiplexer_4 (
    .in0(multiplexer_3_out), .in1(shifter_4_out), .out(multiplexer_4_out), .sel(A[3]));  // open: en
  Shifter #(.width(32), .shift("ar")) shifter_5 (.in(multiplexer_4_out), .\dist (5'b10000), .out(shifter_5_out));
  Multiplexer #(.width(32)) multiplexer_5 (
    .in0(multiplexer_4_out), .in1(shifter_5_out), .out(out), .sel(A[4]));  // open: en
endmodule
